# Fritzing sketch bacteria (saved by Fritzing 0.9.2b)
breadboards: 2

parts:
  Disp1 = LBT2088AH [part_number=LBT2088AH]
  U4 = MAX7219 [package=dil24]
  Part3 = Arduino Uno (Rev3) - ICSP
  Part2 = Thumb Joystick
  U5 = POT [package=pot_alpha_rv16af-20]
  U3 = LCD-16X2 [package=lcd-8x2]
  R1 = Resistor [tolerance=±5% resistance=220 package="2010 [SMD]"]
  R2 = Resistor [tolerance=±5% resistance=10k package="0402 [SMD]"]
  part = Pushbutton [package="[THT]"]

nets:
  N1: Disp1.pin1, U4.DIG0
  N2: Disp1.pin2, U4.DIG4
  N3: Disp1.pin_3, U4.GND
  N4: Disp1.pin_4, U4.DIG6
  N5: Disp1.pin_5, U4.DIG3
  N6: Disp1.pin_6, U4.DIG5
  N7: Disp1.pin_7, U4.DIG1
  N8: Disp1.pin_8, U4.VCC
  N9: Disp1.pin_9, U4.LOAD
  N10: Disp1.pin_10, U4.SEGA
  N11: Disp1.pin_11, U4.SEGF
  N12: Disp1.pin_12, U4.SEGB
  N13: Disp1.pin_13, U4.SEGG
  N14: Disp1.pin_14, U4.SEGC
  N15: Disp1.pin_15, U4.ISET
  N16: Disp1.pin_16, U4.SEGDP
  N17: U4.DIN, Part3.D7
  GND: U4.DIG2, U4.DIG7, Part3.GND, Part2.GND, U5.A, U3.VSS, U3.K
  N18: U4.GND2, Part3.D5_PWM
  N19: U4.CLK, Part3.D6_PWM
  5V: U4.SEGE, Part3.5V, Part3.D4, Part2.VCC, U5.E, U3.VDD, R1.Pin_0, R2.Pin_1, part.Pin_3, part.Pin_4
  N20: U4.SEGD, R2.Pin_0
  N21: Part3.A0, Part2.HORZ
  N22: Part3.A1, Part2.VERT
  N23: Part3.A2, Part2.SEL
  N24: Part3.D8, U3.DB4
  N25: Part3.D9_PWM, U3.DB5
  N26: Part3.D10_PWM/SS, U3.DB6
  N27: Part3.D11_PWM/MOSI, U3.DB7
  N28: Part3.D12/MISO, U3.R_W
  N29: Part3.D13/SCK, U3.RS
  N30: U5.S, U3.VO
  N31: U3.A, R1.Pin_1
